// Logisim project S1-30-Final-final_circuit.circ as structural Verilog: 1 circuit, main circuit main
module main (
  output out_1,
  output out_2
);

  wire and_1_out, and_2_out, and_3_out, and_4_out, and_5_out, and_6_out, and_7_out, and_8_out, and_9_out,
       and_10_out, and_11_out, and_12_out, and_13_out, and_14_out, and_15_out, and_16_out, and_17_out,
       d_ff_1_q, d_ff_2_q, d_ff_3_q, d_ff_4_q, d_ff_5_q, d_ff_6_q, d_ff_7_q, d_ff_8_q, d_ff_9_q, d_ff_10_q,
       d_ff_11_q, d_ff_12_q, d_ff_13_q, d_ff_14_q, d_ff_15_q, d_ff_16_q, d_ff_17_q, d_ff_18_q, d_ff_19_q,
       d_ff_20_q, d_ff_21_q, d_ff_22_q, d_ff_23_q, d_ff_24_q, d_ff_25_q, d_ff_26_q, d_ff_27_q, Draw_out,
       nor_1_out, not_1_out, not_2_out, not_3_out, Reset_out, X1_out, X2_out, X3_out, X4_out, X5_out, X6_out,
       X7_out, X8_out, X9_out, xor_1_out, xor_2_out, xor_3_out, xor_4_out, xor_5_out, xor_6_out, xor_7_out,
       xor_8_out, xor_9_out, xor_10_out;

  Button X1 (.out(X1_out));
  LED led_1 (.in(d_ff_4_q));
  LED led_2 (.in(d_ff_5_q));
  Button X4 (.out(X4_out));
  LED led_3 (.in(d_ff_6_q));
  LED led_4 (.in(d_ff_7_q));
  Button X7 (.out(X7_out));
  LED led_5 (.in(d_ff_8_q));
  LED led_6 (.in(d_ff_9_q));
  LED led_7 (.in(d_ff_13_q));
  LED led_8 (.in(d_ff_14_q));
  Button X5 (.out(X5_out));
  LED led_9 (.in(d_ff_15_q));
  LED led_10 (.in(d_ff_16_q));
  LED led_11 (.in(d_ff_17_q));
  LED led_12 (.in(d_ff_18_q));
  Button X2 (.out(X2_out));
  LED led_13 (.in(d_ff_22_q));
  LED led_14 (.in(d_ff_23_q));
  LED led_15 (.in(d_ff_24_q));
  LED led_16 (.in(d_ff_25_q));
  Button X8 (.out(X8_out));
  LED led_17 (.in(d_ff_26_q));
  LED led_18 (.in(d_ff_27_q));
  Button X3 (.out(X3_out));
  LED led_19 (.in(out_1));
  Button X6 (.out(X6_out));
  Button X9 (.out(X9_out));
  LED led_20 (.in(out_2));
  LED led_21 (.in(Draw_out));
  xor xor_1 (xor_1_out, xor_2_out, xor_3_out, xor_4_out, xor_5_out, xor_6_out, xor_7_out, xor_8_out, xor_9_out, xor_10_out);
  Button Reset (.out(Reset_out));
  not not_1 (not_1_out, xor_1_out);
  D_Flip_Flop d_ff_1 (.clk(X1_out), .D(and_1_out), .Q(d_ff_1_q), .reset(Reset_out));  // open: Qn, preset, en
  D_Flip_Flop d_ff_2 (.clk(X4_out), .D(and_1_out), .Q(d_ff_2_q), .reset(Reset_out));  // open: Qn, preset, en
  D_Flip_Flop d_ff_3 (.clk(X7_out), .D(and_1_out), .Q(d_ff_3_q), .reset(Reset_out));  // open: Qn, preset, en
  D_Flip_Flop d_ff_4 (.clk(d_ff_1_q), .D(not_1_out), .Q(d_ff_4_q), .reset(Reset_out));  // open: Qn, preset, en
  D_Flip_Flop d_ff_5 (.clk(d_ff_1_q), .D(xor_1_out), .Q(d_ff_5_q), .reset(Reset_out));  // open: Qn, preset, en
  D_Flip_Flop d_ff_6 (.clk(d_ff_2_q), .D(not_1_out), .Q(d_ff_6_q), .reset(Reset_out));  // open: Qn, preset, en
  D_Flip_Flop d_ff_7 (.clk(d_ff_2_q), .D(xor_1_out), .Q(d_ff_7_q), .reset(Reset_out));  // open: Qn, preset, en
  D_Flip_Flop d_ff_8 (.clk(d_ff_3_q), .D(not_1_out), .Q(d_ff_8_q), .reset(Reset_out));  // open: Qn, preset, en
  D_Flip_Flop d_ff_9 (.clk(d_ff_3_q), .D(xor_1_out), .Q(d_ff_9_q), .reset(Reset_out));  // open: Qn, preset, en
  xor xor_2 (xor_2_out, d_ff_4_q, d_ff_5_q);
  xor xor_3 (xor_3_out, d_ff_6_q, d_ff_7_q);
  xor xor_4 (xor_4_out, d_ff_8_q, d_ff_9_q);
  D_Flip_Flop d_ff_10 (.clk(X2_out), .D(and_1_out), .Q(d_ff_10_q), .reset(Reset_out));  // open: Qn, preset, en
  D_Flip_Flop d_ff_11 (.clk(X5_out), .D(and_1_out), .Q(d_ff_11_q), .reset(Reset_out));  // open: Qn, preset, en
  D_Flip_Flop d_ff_12 (.clk(X8_out), .D(and_1_out), .Q(d_ff_12_q), .reset(Reset_out));  // open: Qn, preset, en
  D_Flip_Flop d_ff_13 (.clk(d_ff_10_q), .D(not_1_out), .Q(d_ff_13_q), .reset(Reset_out));  // open: Qn, preset, en
  D_Flip_Flop d_ff_14 (.clk(d_ff_10_q), .D(xor_1_out), .Q(d_ff_14_q), .reset(Reset_out));  // open: Qn, preset, en
  D_Flip_Flop d_ff_15 (.clk(d_ff_11_q), .D(not_1_out), .Q(d_ff_15_q), .reset(Reset_out));  // open: Qn, preset, en
  D_Flip_Flop d_ff_16 (.clk(d_ff_11_q), .D(xor_1_out), .Q(d_ff_16_q), .reset(Reset_out));  // open: Qn, preset, en
  D_Flip_Flop d_ff_17 (.clk(d_ff_12_q), .D(not_1_out), .Q(d_ff_17_q), .reset(Reset_out));  // open: Qn, preset, en
  D_Flip_Flop d_ff_18 (.clk(d_ff_12_q), .D(xor_1_out), .Q(d_ff_18_q), .reset(Reset_out));  // open: Qn, preset, en
  xor xor_5 (xor_5_out, d_ff_13_q, d_ff_14_q);
  xor xor_6 (xor_6_out, d_ff_15_q, d_ff_16_q);
  xor xor_7 (xor_7_out, d_ff_17_q, d_ff_18_q);
  D_Flip_Flop d_ff_19 (.clk(X3_out), .D(and_1_out), .Q(d_ff_19_q), .reset(Reset_out));  // open: Qn, preset, en
  D_Flip_Flop d_ff_20 (.clk(X6_out), .D(and_1_out), .Q(d_ff_20_q), .reset(Reset_out));  // open: Qn, preset, en
  D_Flip_Flop d_ff_21 (.clk(X9_out), .D(and_1_out), .Q(d_ff_21_q), .reset(Reset_out));  // open: Qn, preset, en
  D_Flip_Flop d_ff_22 (.clk(d_ff_19_q), .D(not_1_out), .Q(d_ff_22_q), .reset(Reset_out));  // open: Qn, preset, en
  D_Flip_Flop d_ff_23 (.clk(d_ff_19_q), .D(xor_1_out), .Q(d_ff_23_q), .reset(Reset_out));  // open: Qn, preset, en
  D_Flip_Flop d_ff_24 (.clk(d_ff_20_q), .D(not_1_out), .Q(d_ff_24_q), .reset(Reset_out));  // open: Qn, preset, en
  D_Flip_Flop d_ff_25 (.clk(d_ff_20_q), .D(xor_1_out), .Q(d_ff_25_q), .reset(Reset_out));  // open: Qn, preset, en
  D_Flip_Flop d_ff_26 (.clk(d_ff_21_q), .D(not_1_out), .Q(d_ff_26_q), .reset(Reset_out));  // open: Qn, preset, en
  D_Flip_Flop d_ff_27 (.clk(d_ff_21_q), .D(xor_1_out), .Q(d_ff_27_q), .reset(Reset_out));  // open: Qn, preset, en
  xor xor_8 (xor_8_out, d_ff_22_q, d_ff_23_q);
  xor xor_9 (xor_9_out, d_ff_24_q, d_ff_25_q);
  xor xor_10 (xor_10_out, d_ff_26_q, d_ff_27_q);
  and and_1 (and_1_out, 1'b1, nor_1_out);
  and and_2 (and_2_out, d_ff_4_q, d_ff_13_q, d_ff_22_q);
  and and_3 (and_3_out, d_ff_6_q, d_ff_15_q, d_ff_24_q);
  and and_4 (and_4_out, d_ff_4_q, d_ff_6_q, d_ff_8_q);
  and and_5 (and_5_out, d_ff_8_q, d_ff_17_q, d_ff_26_q);
  and and_6 (and_6_out, d_ff_13_q, d_ff_15_q, d_ff_17_q);
  and and_7 (and_7_out, d_ff_22_q, d_ff_24_q, d_ff_26_q);
  and and_8 (and_8_out, d_ff_4_q, d_ff_15_q, d_ff_26_q);
  and and_9 (and_9_out, d_ff_22_q, d_ff_15_q, d_ff_8_q);
  and and_10 (and_10_out, d_ff_5_q, d_ff_14_q, d_ff_23_q);
  and and_11 (and_11_out, d_ff_7_q, d_ff_16_q, d_ff_25_q);
  and and_12 (and_12_out, d_ff_9_q, d_ff_18_q, d_ff_27_q);
  and and_13 (and_13_out, d_ff_5_q, d_ff_7_q, d_ff_9_q);
  and and_14 (and_14_out, d_ff_14_q, d_ff_16_q, d_ff_18_q);
  and and_15 (and_15_out, d_ff_23_q, d_ff_25_q, d_ff_27_q);
  and and_16 (and_16_out, d_ff_5_q, d_ff_16_q, d_ff_27_q);
  and and_17 (and_17_out, d_ff_23_q, d_ff_16_q, d_ff_9_q);
  nor nor_1 (nor_1_out, out_2, out_1);
  or or_1 (out_1, and_2_out, and_3_out, and_4_out, and_5_out, and_6_out, and_7_out, and_8_out, and_9_out);
  or or_2 (out_2, and_10_out, and_11_out, and_12_out, and_13_out, and_14_out, and_15_out, and_16_out, and_17_out);
  not not_2 (not_2_out, out_1);
  not not_3 (not_3_out, out_2);
  and Draw (Draw_out, xor_10_out, xor_9_out, xor_2_out, xor_4_out, xor_3_out, xor_5_out, xor_6_out, xor_7_out, xor_8_out, not_2_out, not_3_out);

  // Notes on the sheet:
  //   Winner
  //   Draw
  //   Resets
  //   Draw
  //   X2 Player 1
  //   X1 Player 1
  //   X3 Player 1
  //   X4 P1
  //   X5 P1
  //   X6 P1
  //   X7 P1
  //   X8 P1
  //   X9 P1
  //   X6 P2
  //   X5 P2
  //   X3 Player 2
  //   X2 Player 2
  //   X1 Player 2
  //   X4 P2
  //   X7 P2
  //   X8 P2
  //   X9 P2
endmodule
